# Fritzing sketch Sketch (saved by Fritzing 0.9.3b)
breadboards: 1

parts:
  Raspberry_Pi1 = Raspberry Pi B+
  U1 = SUP500F [package=sup500f]
  J1 = Piezo Speaker

nets:
  N1: Raspberry_Pi1.3v3, U1.RX-I
  N2: Raspberry_Pi1.GPIO21, J1.pin2
  N3: Raspberry_Pi1.GPIO15, U1.VCC
  N4: Raspberry_Pi1.GPIO14, U1.GND
  N5: Raspberry_Pi1.GND, U1.TX-O, J1.pin1
